# Fritzing sketch GC_Ardugem_Circuit_Diagram (saved by Fritzing 0.9.3b)
breadboards: 1

parts:
  Part1 = Arduino Uno (Rev3)
  Part5 = Triple Axis Accelerometer Breakout - ADXL345
  TFT1 = 1.44" SPI TFT Graphics Display 128x128 [package=THT]

nets:
  N1: Part1.A4/SDA, Part5.SDA
  N2: Part1.A5/SCL, Part5.SCL
  N3: Part1.D9_PWM, TFT1.pin9
  N4: Part1.D10_PWM/SS, TFT1.pin11
  N5: Part1.D11_PWM/MOSI, TFT1.pin8
  N6: Part1.D12/MISO, TFT1.pin10
  N7: Part1.D13/SCK, TFT1.pin7
  GND: Part1.GND, Part5.GND, TFT1.pin2
  N8: Part1.3V3, TFT1.pin6
  5V: Part1.5V, Part5.VCC, TFT1.pin1

custom parts:
  1.44" SPI TFT Graphics Display 128x128: This is for https://www.amazon.com/gp/product/B07B4BDWCL/ref=ask_ql_qh_dp_hza display. Note that this display is sold with a misprinted silkscreen indicating I2C connections on P2 connector, it is actualy SPI. The P1 connections are non functional on this board from the linked URL seller on Amazon.
